# Fritzing sketch sketch (saved by Fritzing 0.9.2b)
breadboards: 1

parts:
  Part1 = Arduino Uno (Rev3) - ICSP
  J1 = Piezo Speaker  # not connected
  J2 = Piezo Speaker  # not connected
  Part2 = Logic Level Converter  # not connected
  S1 = JOYSTICK_MINI [package=joystick_mini]  # not connected
  R1 = Resistor [tolerance=±5% resistance=220 package=THT]
  R2 = Resistor [tolerance=±5% resistance=220 package="0805 [SMD]"]
  R3 = Resistor [tolerance=±5% resistance=220 package="0805 [SMD]"]
  R4 = Resistor [tolerance=±5% resistance=220 package="0805 [SMD]"]
  R5 = Resistor [tolerance=±5% resistance=220 package="0805 [SMD]"]
  R6 = Resistor [tolerance=±5% resistance=220 package="0805 [SMD]"]

nets:
  N1: Part1.D9_PWM, R5.Pin_0
  N2: Part1.D7, R3.Pin_1
  N3: R1.Pin_0, R6.Pin_1
  N4: R1.Pin_1, R2.Pin_0
  N5: R2.Pin_1, R3.Pin_0
  N6: R4.Pin_0, R5.Pin_1
  N7: R4.Pin_1, R6.Pin_0
